# Fritzing sketch Controlling LED by Button (saved by Fritzing 0.9.3b)
breadboards: 1

parts:
  R2 = Resistor [tolerance=±5% resistance=10k package=THT]
  KEY = Pushbutton [package="[THT]"]
  元件1 = Arduino Uno (Rev3) - ICSP

nets:
  N1: R2.Pin_0, KEY.Pin_3, KEY.Pin_4, 元件1.D12/MISO
  N2: R2.Pin_1, 元件1.GND
  N3: KEY.Pin_1, KEY.Pin_2, 元件1.5V

notes:
  www.thingerbits.lk
