# Fritzing sketch RGB LED (saved by Fritzing 0.9.3b)
breadboards: 1

parts:
  R1 = Resistor [tolerance=±5% resistance=220 package=THT]
  R2 = Resistor [tolerance=±5% resistance=220 package=THT]
  R3 = Resistor [tolerance=±5% resistance=220 package=THT]
  LED1 = RGB LED (com. anode, rbg) [package="5 mm [THT]"]
  元件1 = Arduino Uno (Rev3) - ICSP

nets:
  N1: R1.Pin_0, 元件1.D11_PWM/MOSI
  N2: R1.Pin_1, LED1.red_cathode
  N3: R2.Pin_0, 元件1.D9_PWM
  N4: R2.Pin_1, LED1.green_cathode
  N5: R3.Pin_0, 元件1.D10_PWM/SS
  N6: R3.Pin_1, LED1.blue_cathode
  N7: LED1.common_anode, 元件1.GND

notes:
  www.thingerbits.lk
