# Fritzing sketch RGB LED (saved by Fritzing 0.9.3b)
breadboards: 1

parts:
  元件1 = Arduino Uno (Rev3) - ICSP
  T1 = LM35 Temperature Sensor [package="TO92 [THT]"]

nets:
  N1: 元件1.A1, T1.Vout
  GND: 元件1.GND, T1.GND
  N2: 元件1.5V, T1.+Vs

notes:
  www.thingerbits.lk
