# Fritzing sketch Reed-switch (saved by Fritzing 0.9.3b)
breadboards: 1

parts:
  元件1 = Arduino Uno (Rev3) - ICSP
  S1 = SWITCH-MOMENTARY-2 [package=reed_switch_plastic]
  R1 = Resistor [tolerance=±5% resistance=1k package="1206 [SMD]"]
  LED1 = smd LED [color="Red (633nm)" package="0603 [SMD]"]
  R2 = Resistor [tolerance=±5% resistance=220 package=THT]

nets:
  N1: 元件1.D9_PWM, R2.Pin_0
  N2: 元件1.D4, S1.1, R1.Pin_1
  N3: 元件1.5V, R1.Pin_0
  N4: 元件1.GND, S1.2, LED1.anode
  N5: LED1.cathode, R2.Pin_1

notes:
  www.thingerbits.lk
